# Fritzing sketch Glove_schematic (saved by Fritzing 0.9.3b)

parts:
  Part1 = Adafruit Flora [part_number="Adafruit #659"]
  Part2 = Flora LSM303 Compass+Accel
  Part4 = Adafruit MMA8451 Accelerometer [part_number="Adafruit #2019"]
  Part3 = Adafruit MMA8451 Accelerometer [part_number="Adafruit #2019"]

nets:
  N1: Part1.+3V3, Part3.SA0
  GND: Part1.GND, Part2.GND, Part4.GND, Part3.GND
  N2: Part1.IO2/SDA, Part2.SCL, Part4.SCL, Part3.SCL
  N3: Part1.IO3/SCL, Part2.SDA, Part4.SDA, Part3.SDA
  VIN: Part2.3.3V, Part4.VIN, Part3.VIN

custom parts:
  Adafruit Flora: FLORA is Adafruit's fully-featured wearable electronics platform. It's a round, sewable, Arduino-compatible microcontroller designed to empower amazing wearables projects. The FLORA is small (1.75" diameter, weighing 4.4 grams). The FLORA has built-in USB support. Built in USB means you plug it in to program it, it just shows up - all you need is a Micro-B USB cable, no additional purchases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
  Flora LSM303 Compass+Accel: Add motion and direction sensing to your wearable FLORA project with this high precision 3-axis Accelerometer+Compass sensor. Inside are two sensors, one is a classic 3-axis accelerometer, which can tell you which direction is down towards the Earth (by measuring gravity) or how fast the board is accelerating in 3D space. The other is a magnetometer that can sense where the strongest magnetic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
  Adafruit MMA8451 Accelerometer: So many accelerometers and so little time! We've expanded our accelerometer selection even more with this high-precision and inexpensive MMA8451 Triple-Axis Accelerometer w/ 14-bit ADC. You can detect motion, tilt and basic orientation with a digital accelerometer - and the MMA8451 is a great accelerometer to start with. It has a wide usage range, from +-2g up to +-8g yet is easy to use with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
